# Fritzing sketch CE301_Midterm2_Transmitter (saved by Fritzing 0.9.3b)
breadboards: 1

parts:
  U1 = atmega328 [package=dip]
  T1 = LM34 Temperature Sensor [package="TO92 [THT]"]
  Part1 = NRF24L01
  V1 = DC Power [voltage=3.3V]

nets:
  N1: U1.D0_(RX), T1.Vout
  N2: U1.D2, Part1.IRQ
  N3: U1.AVCC, T1.+Vs
  GND: U1.GND, T1.GND, Part1.GND, V1.V-
  N4: U1.A1, Part1.CE
  N5: U1.A2, Part1.CSN
  N6: U1.A3, Part1.MOSI
  N7: U1.A4, Part1.MISO
  N8: U1.A5, Part1.SCK
  N9: Part1.VCC, V1.V+
