# Fritzing sketch CPE301_ArduinoMega2560_Receiver (saved by Fritzing 0.9.3b)
breadboards: 1

parts:
  Part3 = Arduino Mega 2560 (Rev3)
  Part4 = NRF24L01+ Breakout Board
  BAT2 = Battery Holders [package=battery]
  T1 = LM34 Temperature Sensor [package="TO92 [THT]"]

nets:
  N1: Part3.A0, T1.Vout
  GND: Part3.GND, Part4.GND, BAT2.-, T1.GND
  N2: Part3.5V, T1.+Vs
  N3: Part3.D48, Part4.CS
  N4: Part3.D50, Part4.MISO
  N5: Part3.D51, Part4.MOSI
  N6: Part3.D52, Part4.SCK
  N7: Part3.D53, Part4.CE
  N8: Part4.VCC, BAT2.+
