# Fritzing sketch CPE301_ArduinoMega2560_Transmitter (saved by Fritzing 0.9.3b)
breadboards: 1

parts:
  Part1 = Arduino Mega 2560 (Rev3)
  Part2 = NRF24L01+ Breakout Board
  BAT1 = Battery Holders [package=battery]

nets:
  GND: Part1.GND, Part2.GND, BAT1.-
  N1: Part1.D48, Part2.CS
  N2: Part1.D50, Part2.MISO
  N3: Part1.D51, Part2.MOSI
  N4: Part1.D52, Part2.SCK
  N5: Part1.D53, Part2.CE
  N6: Part2.VCC, BAT1.+
