# Fritzing sketch CPE301_Midterm2_Receiver (saved by Fritzing 0.9.3b)
breadboards: 1

parts:
  U2 = atmega328 [package=dip]
  Part2 = NRF24L01
  V2 = DC Power [voltage=3.3V]

nets:
  N1: U2.D2, Part2.IRQ
  GND: U2.GND, Part2.GND, V2.V-
  N2: U2.A1, Part2.CE
  N3: U2.A2, Part2.CSN
  N4: U2.A3, Part2.MOSI
  N5: U2.A4, Part2.MISO
  N6: U2.A5, Part2.SCK
  N7: Part2.VCC, V2.V+
